# Fritzing sketch Circuito - Sensor DHT22 con ESP8266 (saved by Fritzing 0.9.3b)

parts:
  U1 = ESP8266 NodeMCU LoLin module
  DHT1 = DHT22 Humidity and Temperature Sensor

nets:
  3V3: U1.3V3, DHT1.VDD
  N1: U1.D8, DHT1.DATA
  GND: U1.GND, DHT1.GND

notes:
  Si usas el D8, desconecta el sensor
  al subir el programa, o al abrir el monitor serial. Conéctalo de nuevo cuando se imprima el primer mensaje o el programa se haya cargado

custom parts:
  ESP8266 NodeMCU LoLin module: ESP8266 based NodeMCU
