# Fritzing sketch LED con NodeMCU ESP8266 (saved by Fritzing 0.9.3b)
breadboards: 1

parts:
  U1 = ESP8266 NodeMCU LoLin module
  LED1 = LED - 5mm [color="Red (633nm)" package="5 mm [THT]"]
  R1 = Resistor [tolerance=±5% resistance=220 package=THT]

nets:
  N1: U1.D1, R1.Pin_1
  N2: U1.GND, LED1.cathode
  N3: LED1.anode, R1.Pin_0

custom parts:
  ESP8266 NodeMCU LoLin module: ESP8266 based NodeMCU
